// Logisim project BB_V0.1.circ as structural Verilog: 10 circuits, main circuit main
module main (
  input  in_1,
  input  in_2,
  input  in_3,
  input  in_4,
  input  in_5,
  input  in_6,
  input  in_7,
  input  in_8,
  output out_9,
  output out_10,
  output out_11,
  output out_12,
  output out_13,
  output out_14,
  output out_15,
  output out_16
);

  wire A0Q, A1Q, A2Q, A3Q, A4Q, A5Q, A6Q, A7Q, alu_1_out_19, alu_1_out_21, alu_1_out_23, alu_1_out_25,
       alu_1_out_27, alu_1_out_29, alu_1_out_31, alu_1_out_33, B0Q, B1Q, B2Q, B3Q, B4Q, B5Q, B6Q, B7Q,
       clock_1_out;

  Clock clock_1 (.out(clock_1_out));
  A_register a_register_1 (
    .LOAD_prime(in_3), .out_22(A7Q), ._3Q(A5Q), ._4Q(A4Q), ._5Q(A3Q), ._6Q(A2Q), ._7Q(A1Q), ._8Q_2(A0Q),
    ._8Q(in_5), .out_13(out_9), .out_14(out_10), .out_15(out_11), .out_16(out_12), .out_17(out_13),
    .out_18(out_14), .out_19(out_15), .out_20(out_16), .in_3(out_9), .in_4(out_10), .in_5(out_11),
    .in_6(out_12), .in_7(out_13), .in_8(out_14), .in_9(out_15), .in_10(out_16), .in_1(clock_1_out),
    .in_12(in_4), .out_21(A6Q));
  B_register b_register_1 (
    .in_1(clock_1_out), .LOAD_prime(in_6), .in_3(out_9), .in_4(out_10), .in_5(out_11), .in_6(out_12),
    .in_7(out_13), .in_8(out_14), .in_9(out_15), .in_10(out_16), .out_13(out_9), .out_14(out_10),
    .out_15(out_11), .out_16(out_12), .out_17(out_13), .out_18(out_14), .out_19(out_15), .out_20(out_16),
    ._1Q(B7Q), ._2Q(B6Q), ._3Q(B5Q), ._4Q(B4Q), ._5Q(B3Q), ._6Q(B2Q), ._7Q(B1Q), ._8Q_2(B0Q), ._8Q(in_8),
    .in_12(in_7));
  LED led_1 (.in(A7Q));
  LED led_2 (.in(A5Q));
  LED led_3 (.in(A6Q));
  LED led_4 (.in(B7Q));
  LED led_5 (.in(B5Q));
  LED led_6 (.in(B6Q));
  LED led_7 (.in(A3Q));
  LED led_8 (.in(A4Q));
  LED led_9 (.in(A1Q));
  LED led_10 (.in(A2Q));
  LED led_11 (.in(B3Q));
  LED led_12 (.in(B1Q));
  LED led_13 (.in(B2Q));
  LED led_14 (.in(B4Q));
  LED led_15 (.in(A0Q));
  LED led_16 (.in(B0Q));
  ALU alu_1 (
    .in_9(in_1), .in_10(in_2), .out_19(alu_1_out_19), .out_20(out_9), .out_21(alu_1_out_21), .out_22(out_10),
    .out_23(alu_1_out_23), .out_24(out_11), .out_25(alu_1_out_25), .out_26(out_12), .out_27(alu_1_out_27),
    .out_28(out_13), .out_29(alu_1_out_29), .out_30(out_14), .out_31(alu_1_out_31), .out_32(out_15),
    .out_33(alu_1_out_33), .out_34(out_16), .in_1(A7Q), .in_2(A6Q), .in_3(A5Q), .in_4(A4Q), .in_5(A3Q),
    .in_6(A2Q), .in_7(A1Q), .in_8(A0Q), .in_11(B7Q), .in_12(B6Q), .in_13(B5Q), .in_14(B4Q), .in_15(B3Q),
    .in_16(B2Q), .in_17(B1Q), .in_18(B0Q));
  LED led_17 (.in(alu_1_out_19));
  LED led_18 (.in(alu_1_out_21));
  LED led_19 (.in(alu_1_out_23));
  LED led_20 (.in(alu_1_out_31));
  LED led_21 (.in(alu_1_out_29));
  LED led_22 (.in(alu_1_out_25));
  LED led_23 (.in(alu_1_out_27));
  LED led_24 (.in(alu_1_out_33));

  // Other names for the same wires on the sheet: B0 = out_16; B1 = out_15; B2 = out_14; B3 = out_13; B4 = out_12;
  //   B5 = out_11; B6 = out_10; B7 = out_9
endmodule

module Clock_Module (
  input  HLT,
  output CLK
);

  wire clock_1_out, not_1_out;

  Clock clock_1 (.out(clock_1_out));
  not not_1 (not_1_out, HLT);
  and and_1 (CLK, clock_1_out, not_1_out);

  // Notes on the sheet:
  //   Clock Module
endmodule

module D_FLIPFLOP (
  input  in_1,
  input  CLK,
  input  D,
  output Q
);

  wire and_1_out, and_2_out, and_3_out, nor_2_out, not_1_out, not_2_out, not_3_out, not_4_out, not_5_out;

  not not_1 (not_1_out, not_2_out);
  not not_2 (not_2_out, CLK);
  not not_3 (not_3_out, not_1_out);
  and and_1 (and_1_out, CLK, not_3_out);
  not not_4 (not_4_out, D);
  not not_5 (not_5_out, in_1);
  and and_2 (and_2_out, not_4_out, and_1_out);
  and and_3 (and_3_out, and_1_out, D);
  nor nor_1 (Q, not_5_out, and_2_out, nor_2_out);
  nor nor_2 (nor_2_out, Q, and_3_out);

  // Notes on the sheet:
  //   S
  //   Q
endmodule

module D_FF_WITH_LOAD (
  input  in_1,
  input  in_2,
  input  in_3,
  input  in_4,
  output out_5
);

  wire and_1_out, and_2_out, not_1_out, or_1_out;

  and and_1 (and_1_out, out_5, in_2);
  not not_1 (not_1_out, in_2);
  and and_2 (and_2_out, not_1_out, in_3);
  or or_1 (or_1_out, and_1_out, and_2_out);
  D_FLIPFLOP d_flipflop_1 (.CLK(in_1), .D(or_1_out), .Q(out_5), .in_1(in_4));
endmodule

module _8_BIT_REGISTER (
  input  in_1,
  input  LOAD_prime,
  input  _1D,
  input  _2D,
  input  _3D,
  input  _4D,
  input  _5D,
  input  _6D,
  input  _7D,
  input  _8D,
  input  in_11,
  output out_12,
  output out_13,
  output out_14,
  output out_15,
  output out_16,
  output out_17,
  output out_18,
  output out_19
);

  Pull_Resistor #(.pull(1)) pull_resistor_1 (.node(_1D));
  D_FF_WITH_LOAD d_ff_with_load_1 (.in_1(in_1), .in_3(_1D), .in_4(in_11), .in_2(LOAD_prime), .out_5(out_12));
  Pull_Resistor #(.pull(1)) pull_resistor_2 (.node(_2D));
  D_FF_WITH_LOAD d_ff_with_load_2 (.in_1(in_1), .in_3(_2D), .in_4(in_11), .in_2(LOAD_prime), .out_5(out_13));
  D_FF_WITH_LOAD d_ff_with_load_3 (.in_1(in_1), .in_3(_3D), .in_4(in_11), .in_2(LOAD_prime), .out_5(out_14));
  Pull_Resistor #(.pull(1)) pull_resistor_3 (.node(_3D));
  Pull_Resistor #(.pull(1)) pull_resistor_4 (.node(_4D));
  D_FF_WITH_LOAD d_ff_with_load_4 (.in_1(in_1), .in_3(_4D), .in_4(in_11), .in_2(LOAD_prime), .out_5(out_15));
  Pull_Resistor #(.pull(1)) pull_resistor_5 (.node(_5D));
  D_FF_WITH_LOAD d_ff_with_load_5 (.in_1(in_1), .in_3(_5D), .in_4(in_11), .in_2(LOAD_prime), .out_5(out_16));
  Pull_Resistor #(.pull(1)) pull_resistor_6 (.node(_6D));
  D_FF_WITH_LOAD d_ff_with_load_6 (.in_1(in_1), .in_3(_6D), .in_4(in_11), .in_2(LOAD_prime), .out_5(out_17));
  Pull_Resistor #(.pull(1)) pull_resistor_7 (.node(_7D));
  D_FF_WITH_LOAD d_ff_with_load_7 (.in_1(in_1), .in_3(_7D), .in_4(in_11), .in_2(LOAD_prime), .out_5(out_18));
  Pull_Resistor #(.pull(1)) pull_resistor_8 (.node(_8D));
  D_FF_WITH_LOAD d_ff_with_load_8 (.in_1(in_1), .in_3(_8D), .in_4(in_11), .in_2(LOAD_prime), .out_5(out_19));
endmodule

module A_register (
  input  in_1,
  input  LOAD_prime,
  input  in_3,
  input  in_4,
  input  in_5,
  input  in_6,
  input  in_7,
  input  in_8,
  input  in_9,
  input  in_10,
  input  _8Q,
  input  in_12,
  output out_13,
  output out_14,
  output out_15,
  output out_16,
  output out_17,
  output out_18,
  output out_19,
  output out_20,
  output out_21,
  output out_22,
  output _3Q,
  output _4Q,
  output _5Q,
  output _6Q,
  output _7Q,
  output _8Q_2
);

  wire not_1_out;

  _8_BIT_REGISTER u_8_bit_register_1 (
    .LOAD_prime(LOAD_prime), ._1D(in_3), ._2D(in_4), ._3D(in_5), ._4D(in_6), ._5D(in_7), ._6D(in_8),
    ._7D(in_9), ._8D(in_10), .out_12(out_21), .out_13(out_22), .out_16(_5Q), .out_17(_6Q), .out_18(_7Q),
    .out_19(_8Q_2), .in_11(in_12), .out_15(_4Q), .out_14(_3Q), .in_1(in_1));
  assign out_13 = not_1_out ? out_21 : 1'bz;  // Controlled_Buffer controlled_buffer_1
  assign out_14 = not_1_out ? out_22 : 1'bz;  // Controlled_Buffer controlled_buffer_2
  assign out_15 = not_1_out ? _3Q : 1'bz;  // Controlled_Buffer controlled_buffer_3
  assign out_16 = not_1_out ? _4Q : 1'bz;  // Controlled_Buffer controlled_buffer_4
  assign out_17 = not_1_out ? _5Q : 1'bz;  // Controlled_Buffer controlled_buffer_5
  assign out_18 = not_1_out ? _6Q : 1'bz;  // Controlled_Buffer controlled_buffer_6
  assign out_19 = not_1_out ? _7Q : 1'bz;  // Controlled_Buffer controlled_buffer_7
  assign out_20 = not_1_out ? _8Q_2 : 1'bz;  // Controlled_Buffer controlled_buffer_8
  not not_1 (not_1_out, _8Q);
endmodule

module B_register (
  input  in_1,
  input  LOAD_prime,
  input  in_3,
  input  in_4,
  input  in_5,
  input  in_6,
  input  in_7,
  input  in_8,
  input  in_9,
  input  in_10,
  input  _8Q,
  input  in_12,
  output out_13,
  output out_14,
  output out_15,
  output out_16,
  output out_17,
  output out_18,
  output out_19,
  output out_20,
  output _1Q,
  output _2Q,
  output _3Q,
  output _4Q,
  output _5Q,
  output _6Q,
  output _7Q,
  output _8Q_2
);

  wire not_1_out;

  _8_BIT_REGISTER u_8_bit_register_1 (
    .LOAD_prime(LOAD_prime), ._1D(in_3), ._2D(in_4), ._3D(in_5), ._4D(in_6), ._5D(in_7), ._6D(in_8),
    ._7D(in_9), ._8D(in_10), .out_12(_1Q), .out_13(_2Q), .out_16(_5Q), .out_17(_6Q), .out_18(_7Q),
    .out_19(_8Q_2), .in_11(in_12), .out_15(_4Q), .out_14(_3Q), .in_1(in_1));
  assign out_13 = not_1_out ? _1Q : 1'bz;  // Controlled_Buffer controlled_buffer_1
  assign out_14 = not_1_out ? _2Q : 1'bz;  // Controlled_Buffer controlled_buffer_2
  assign out_15 = not_1_out ? _3Q : 1'bz;  // Controlled_Buffer controlled_buffer_3
  assign out_16 = not_1_out ? _4Q : 1'bz;  // Controlled_Buffer controlled_buffer_4
  assign out_17 = not_1_out ? _5Q : 1'bz;  // Controlled_Buffer controlled_buffer_5
  assign out_18 = not_1_out ? _6Q : 1'bz;  // Controlled_Buffer controlled_buffer_6
  assign out_19 = not_1_out ? _7Q : 1'bz;  // Controlled_Buffer controlled_buffer_7
  assign out_20 = not_1_out ? _8Q_2 : 1'bz;  // Controlled_Buffer controlled_buffer_8
  not not_1 (not_1_out, _8Q);
endmodule

module Fast_Carry_Adder (
  input  A,
  input  B,
  input  Cin,
  output pi,
  output Gi,
  output S
);

  and and_1 (pi, A, B);
  xor xor_1 (Gi, B, A);
  xor xor_2 (S, Cin, Gi);
endmodule

module _8_bit_fast_carry_adder (
  input  in_1,
  input  in_2,
  input  in_3,
  input  in_4,
  input  in_5,
  input  in_6,
  input  in_7,
  input  in_8,
  input  in_9,
  input  in_10,
  output out_11,
  output out_12,
  output out_13,
  output out_14,
  output out_15,
  output out_16,
  output out_17,
  output out_18,
  output out_19
);

  wire and_1_out, and_2_out, and_3_out, and_4_out, and_5_out, and_6_out, and_7_out, C1, C2, C3, G0, G1, G2,
       G3, P0, P1, P2, P3;

  Fast_Carry_Adder fast_carry_adder_1 (.A(in_1), .B(in_7), .Cin(in_6), .S(out_16), .Gi(P0), .pi(G0));
  and and_1 (and_1_out, P0, in_6);
  xor xor_1 (C1, G0, and_1_out);
  Fast_Carry_Adder fast_carry_adder_2 (.A(in_2), .B(in_8), .Cin(C1), .S(out_17), .Gi(P1), .pi(G1));
  and and_2 (and_2_out, P1, C1);
  xor xor_2 (C2, G1, and_2_out);
  Fast_Carry_Adder fast_carry_adder_3 (.A(in_3), .B(in_9), .Cin(C2), .S(out_18), .Gi(P2), .pi(G2));
  and and_3 (and_3_out, P2, G1);
  ExactlyOne xor_3 (.out(C3), .in0(G2), .in1(and_3_out), .in2(and_4_out));
  and and_4 (and_4_out, P2, P1, C1);
  Fast_Carry_Adder fast_carry_adder_4 (.A(in_4), .B(in_10), .Cin(C3), .S(out_19), .Gi(P3), .pi(G3));
  and and_5 (and_5_out, P3, G2);
  ExactlyOne xor_4 (.out(out_11), .in0(G3), .in1(and_5_out), .in2(and_6_out), .in3(and_7_out));
  and and_6 (and_6_out, P2, P3, G1);
  assign out_12 = in_5 ? out_19 : 1'bz;  // Controlled_Buffer controlled_buffer_1
  assign out_13 = in_5 ? out_18 : 1'bz;  // Controlled_Buffer controlled_buffer_2
  assign out_14 = in_5 ? out_17 : 1'bz;  // Controlled_Buffer controlled_buffer_3
  assign out_15 = in_5 ? out_16 : 1'bz;  // Controlled_Buffer controlled_buffer_4
  and and_7 (and_7_out, P1, P2, P3, C1);

  // Other names for the same wires on the sheet: A0 = in_1; A1 = in_2; A2 = in_3; A3 = in_4; B0 = in_7; B1 = in_8;
  //   B2 = in_9; B3 = in_10; Cin = in_6; CO = out_11; S0 = out_16; S1 = out_17; S2 = out_18; S3 = out_19
endmodule

module ALU (
  input  in_1,
  input  in_2,
  input  in_3,
  input  in_4,
  input  in_5,
  input  in_6,
  input  in_7,
  input  in_8,
  input  in_9,
  input  in_10,
  input  in_11,
  input  in_12,
  input  in_13,
  input  in_14,
  input  in_15,
  input  in_16,
  input  in_17,
  input  in_18,
  output out_19,
  output out_20,
  output out_21,
  output out_22,
  output out_23,
  output out_24,
  output out_25,
  output out_26,
  output out_27,
  output out_28,
  output out_29,
  output out_30,
  output out_31,
  output out_32,
  output out_33,
  output out_34
);

  wire n8_bit_fast_carry_adder_2_out_11, not_1_out, xor_1_out, xor_2_out, xor_3_out, xor_4_out, xor_5_out,
       xor_6_out, xor_7_out, xor_8_out;

  not not_1 (not_1_out, in_9);
  _8_bit_fast_carry_adder u_8_bit_fast_carry_adder_1 (
    .in_6(n8_bit_fast_carry_adder_2_out_11), .out_12(out_20), .out_13(out_22), .out_14(out_24),
    .out_15(out_26), .in_1(in_4), .in_2(in_3), .in_3(in_2), .in_4(in_1), .in_7(xor_4_out), .in_8(xor_3_out),
    .in_9(xor_2_out), .in_10(xor_1_out), .out_16(out_25), .out_17(out_23), .out_18(out_21), .out_19(out_19),
    .in_5(not_1_out));  // open: out_11
  xor xor_1 (xor_1_out, in_10, in_11);
  xor xor_2 (xor_2_out, in_10, in_12);
  xor xor_3 (xor_3_out, in_10, in_13);
  xor xor_4 (xor_4_out, in_10, in_14);
  _8_bit_fast_carry_adder u_8_bit_fast_carry_adder_2 (
    .in_6(in_10), .out_11(n8_bit_fast_carry_adder_2_out_11), .out_12(out_28), .out_13(out_30),
    .out_14(out_32), .out_15(out_34), .in_1(in_8), .in_2(in_7), .in_3(in_6), .in_4(in_5), .in_7(xor_8_out),
    .in_8(xor_7_out), .in_9(xor_6_out), .in_10(xor_5_out), .out_16(out_33), .out_17(out_31), .out_18(out_29),
    .out_19(out_27), .in_5(not_1_out));
  xor xor_5 (xor_5_out, in_10, in_15);
  xor xor_6 (xor_6_out, in_10, in_16);
  xor xor_7 (xor_7_out, in_10, in_17);
  xor xor_8 (xor_8_out, in_10, in_18);

  // Other names for the same wires on the sheet: BY0 = out_34; BY1 = out_32; BY2 = out_30; BY3 = out_28; BY4 = out_26;
  //   BY5 = out_24; BY6 = out_22; BY7 = out_20; Y0 = out_33; Y1 = out_31; Y2 = out_29; Y3 = out_27; Y4 = out_25;
  //   Y5 = out_23; Y6 = out_21; Y7 = out_19
endmodule
